// Logisim project ROM.circ as structural Verilog: 1 circuit, main circuit main
module main (
  input  in_1,
  input  in_2,
  input  in_3,
  input  in_4,
  input  in_5,
  input  in_6,
  input  in_7,
  input  in_8,
  input  in_9,
  input  in_10
);

  wire [3:0] rom_1_data;
  wire [7:0] rom_2_data;

  DotMatrix #(.matrixcols(3), .matrixrows(4)) dotmatrix_1 (.col0({in_7, in_8, in_9, in_10}));  // open: col1, col2
  // Probe on rom_1_data
  // Probe on rom_1_data
  ROM #(.addrWidth(3), .dataWidth(4)) rom_1 (.addr({in_1, in_2, in_3}), .data(rom_1_data));  // open: sel
  // Probe on rom_2_data
  // Probe on rom_2_data
  ROM #(.addrWidth(3)) rom_2 (.addr({in_4, in_5, in_6}), .data(rom_2_data));  // open: sel

  // Notes on the sheet:
  //   contents of rom_1 (hex, n*v repeats v):
  //   2 4 5 6
endmodule
