// Logisim project ROM2.circ as structural Verilog: 2 circuits, main circuit main
module main (
  input  in_1,
  output [2:0] out_2
);

  wire d_ff_1_qn, d_ff_2_qn, d_ff_3_qn;

  // Probe on out_2
  D_Flip_Flop d_ff_1 (.clk(in_1), .D(d_ff_1_qn), .Q(out_2[0]), .Qn(d_ff_1_qn));  // open: preset, en, reset
  D_Flip_Flop d_ff_2 (.clk(d_ff_1_qn), .D(d_ff_2_qn), .Q(out_2[1]), .Qn(d_ff_2_qn));  // open: preset, en, reset
  D_Flip_Flop d_ff_3 (.clk(d_ff_2_qn), .D(d_ff_3_qn), .Q(out_2[2]), .Qn(d_ff_3_qn));  // open: preset, en, reset
endmodule

module animar (
);

  wire clock_1_out;
  wire [2:0] main_1_out_2;
  wire [8:0] rom_1_data;

  main main_1 (.out_2(main_1_out_2), .in_1(clock_1_out));
  Clock clock_1 (.out(clock_1_out));
  DotMatrix #(.matrixcols(3), .matrixrows(3)) dotmatrix_1 (
    .col0({rom_1_data[0], rom_1_data[1], rom_1_data[2]}),
    .col1({rom_1_data[3], rom_1_data[4], rom_1_data[5]}), .col2({rom_1_data[6], rom_1_data[7], rom_1_data[8]}));
  ROM #(.addrWidth(3), .dataWidth(9)) rom_1 (.addr(main_1_out_2), .data(rom_1_data));  // open: sel
endmodule
