// Logisim project APRENDER.circ as structural Verilog: 3 circuits, main circuit Contadores
module Contadores (
);

  wire clock_1_out, clock_2_out, clock_3_out, d_ff_1_qn, d_ff_2_qn, j_k_ff_1_qn;
  wire [1:0] d_ff_1_q, j_k_ff_1_q, t_ff_1_q;

  Clock clock_1 (.out(clock_1_out));
  // Probe on d_ff_1_q
  D_Flip_Flop d_ff_1 (.clk(clock_1_out), .D(d_ff_1_qn), .Q(d_ff_1_q[0]), .Qn(d_ff_1_qn));  // open: preset, en, reset
  // Probe on t_ff_1_q
  Clock clock_2 (.out(clock_2_out));
  T_Flip_Flop t_ff_1 (.clk(clock_2_out), .T(1'b1), .Q(t_ff_1_q[0]));  // open: Qn, preset, reset, en
  D_Flip_Flop d_ff_2 (.clk(d_ff_1_qn), .D(d_ff_2_qn), .Q(d_ff_1_q[1]), .Qn(d_ff_2_qn));  // open: preset, en, reset
  T_Flip_Flop t_ff_2 (.clk(t_ff_1_q[0]), .T(1'b1), .Q(t_ff_1_q[1]));  // open: Qn, preset, reset, en
  Clock clock_3 (.out(clock_3_out));
  // Probe on j_k_ff_1_q
  J_K_Flip_Flop j_k_ff_1 (
    .J(1'b1), .clk(clock_3_out), .K(1'b1), .Q(j_k_ff_1_q[0]), .Qn(j_k_ff_1_qn));  // open: preset, en, reset
  J_K_Flip_Flop j_k_ff_2 (.J(1'b1), .clk(j_k_ff_1_qn), .K(1'b1), .Q(j_k_ff_1_q[1]));  // open: Qn, preset, en, reset

  // Notes on the sheet:
  //   REGRA
  //   Saiu do Q e foi para o Clock é decrescente 
  //   Saiu do Q barra e foi para o Clock é crescente
endmodule

module Contadores2 (
);

  wire and_1_out, and_2_out, and_3_out, and_4_out, clock_1_out, clock_2_out, clock_3_out, clock_4_out,
       d_ff_1_qn, d_ff_2_qn, d_ff_3_qn, d_ff_4_qn, d_ff_5_qn, d_ff_6_qn, t_ff_1_qn, t_ff_2_qn, t_ff_3_qn,
       t_ff_4_qn, t_ff_5_qn, t_ff_6_qn;
  wire [2:0] d_ff_1_q, d_ff_2_q, t_ff_1_q, t_ff_2_q;

  Clock clock_1 (.out(clock_1_out));
  Clock clock_2 (.out(clock_2_out));
  // Probe on d_ff_1_q
  D_Flip_Flop d_ff_1 (
    .clk(clock_1_out), .D(d_ff_1_qn), .Q(d_ff_1_q[0]), .Qn(d_ff_1_qn), .reset(and_1_out));  // open: preset, en
  // Probe on d_ff_2_q
  D_Flip_Flop d_ff_2 (
    .clk(clock_2_out), .D(d_ff_2_qn), .Q(d_ff_2_q[0]), .Qn(d_ff_2_qn), .reset(and_2_out));  // open: preset, en
  D_Flip_Flop d_ff_3 (
    .clk(d_ff_1_qn), .D(d_ff_3_qn), .Q(d_ff_1_q[1]), .Qn(d_ff_3_qn), .preset(and_1_out));  // open: en, reset
  D_Flip_Flop d_ff_4 (
    .clk(d_ff_2_q[0]), .D(d_ff_4_qn), .Q(d_ff_2_q[1]), .Qn(d_ff_4_qn), .preset(and_2_out));  // open: en, reset
  D_Flip_Flop d_ff_5 (
    .clk(d_ff_3_qn), .D(d_ff_5_qn), .Q(d_ff_1_q[2]), .Qn(d_ff_5_qn), .reset(and_1_out));  // open: preset, en
  D_Flip_Flop d_ff_6 (
    .clk(d_ff_2_q[1]), .D(d_ff_6_qn), .Q(d_ff_2_q[2]), .Qn(d_ff_6_qn), .preset(and_2_out));  // open: en, reset
  and and_1 (and_1_out, d_ff_1_q[2], d_ff_1_q[1], d_ff_1_q[0]);
  and and_2 (and_2_out, d_ff_6_qn, d_ff_4_qn, d_ff_2_q[0]);
  Clock clock_3 (.out(clock_3_out));
  Clock clock_4 (.out(clock_4_out));
  // Probe on t_ff_1_q
  T_Flip_Flop t_ff_1 (
    .clk(clock_3_out), .T(1'b1), .Q(t_ff_1_q[0]), .Qn(t_ff_1_qn), .reset(and_3_out));  // open: preset, en
  // Probe on t_ff_2_q
  T_Flip_Flop t_ff_2 (
    .clk(clock_4_out), .T(1'b1), .Q(t_ff_2_q[0]), .Qn(t_ff_2_qn), .reset(and_4_out));  // open: preset, en
  T_Flip_Flop t_ff_3 (
    .clk(t_ff_1_qn), .T(1'b1), .Q(t_ff_1_q[1]), .Qn(t_ff_3_qn), .preset(and_3_out));  // open: reset, en
  T_Flip_Flop t_ff_4 (
    .clk(t_ff_2_q[0]), .T(1'b1), .Q(t_ff_2_q[1]), .Qn(t_ff_4_qn), .preset(and_4_out));  // open: reset, en
  T_Flip_Flop t_ff_5 (
    .clk(t_ff_3_qn), .T(1'b1), .Q(t_ff_1_q[2]), .Qn(t_ff_5_qn), .reset(and_3_out));  // open: preset, en
  T_Flip_Flop t_ff_6 (
    .clk(t_ff_2_q[1]), .T(1'b1), .Q(t_ff_2_q[2]), .Qn(t_ff_6_qn), .preset(and_4_out));  // open: reset, en
  and and_3 (and_3_out, t_ff_1_q[2], t_ff_1_q[1], t_ff_1_q[0]);
  and and_4 (and_4_out, t_ff_6_qn, t_ff_4_qn, t_ff_2_q[0]);

  // Notes on the sheet:
  //   D
  //   Valor inicial 2 (010) - Vai em baixo
  //   Valor inicial 6 (110) - Vai em baixo
  //   Ex: 2 (010 -> 010)
  //   Valor Final 6 (110) + 1 = 7 (111) - Vai em cima 
  //   Valor Final 2 (010) - 1 = 1 (001) - Vai em cima 
  //   OBS: Lembre-se de Inverter a ordem dos valores finais e iniciais
  //   Ex: 6 (110 -> 011)
  //   T
  //   Valor inicial 2 (010) - Vai em baixo
  //   Valor inicial 6 (110) - Vai em baixo
  //   Valor Final 6 (110) + 1 = 7 (111) - Vai em cima 
  //   Valor Final 2 (010) - 1 = 1 (001) - Vai em cima 
endmodule

module Sincrono (
);

  wire clock_1_out, d_ff_1_qn, d_ff_2_qn, d_ff_3_qn;
  wire [2:0] d_ff_3_q;

  // Probe on d_ff_3_q
  Clock clock_1 (.out(clock_1_out));
  D_Flip_Flop d_ff_1 (.clk(clock_1_out), .Q(d_ff_3_q[2]), .Qn(d_ff_1_qn));  // open: D, preset, en, reset
  D_Flip_Flop d_ff_2 (.Q(d_ff_3_q[1]), .Qn(d_ff_2_qn));  // open: clk, D, preset, en, reset
  D_Flip_Flop d_ff_3 (.Q(d_ff_3_q[0]), .Qn(d_ff_3_qn));  // open: clk, D, preset, en, reset

  // Notes on the sheet:
  //   0, 2, 5,7, 6, 1, 4,3
endmodule
